# Fritzing sketch datalogger (saved by Fritzing 0.9.6b)
circuit board: 8.46667cm x 5.64444cm
breadboards: 1

parts:
  U1 = NodeMCU V1.0
  RJ12_jack = RJ11 Jack [package=rj11-6]
  4*NAND = 4011 4 x 2 Input NAND Gate, single part [part_number=4011 package="DIP (Dual Inline) [THT]"]
  R1 = Resistor [tolerance=±5% resistance=1k package=THT]

nets:
  GND: U1.GND, RJ12_jack.3, RJ12_jack.6, 4*NAND.GND
  N1: U1.D5, RJ12_jack.2
  N2: U1.RX, 4*NAND.Q1
  VIN: U1.Vin, RJ12_jack.1, 4*NAND.A1, 4*NAND.VDD, R1.Pin_1
  N3: RJ12_jack.5, 4*NAND.B1, R1.Pin_0

custom parts:
  NodeMCU V1.0: ESP8266 based NodeMCU
  RJ11 Jack: RJ11 Jack Simple 6 pin RJ11 jack. PCB view (only) modified for Molex 6P6C Right Angle Through Hole RJ11 Socket
